# Fritzing sketch ICNEA (saved by Fritzing 0.9.10b)

parts:
  J1 = Piezo Speaker
  U1 = WS2812 RGB LED matrix 1x8
  Mod2 = Raspberry Pi 4B
  U3 = WS2812 RGB LED matrix 1x8
  J2 = Dagu DGServo 9g header connector (female) [package=THT]
  Power_plug1 = Power plug
  Q2 = npn-Powertransistor [package="TO220 [THT]"]

nets:
  GND: J1.pin1, U1.GND#0, U1.GND#3, Mod2.GND, Power_plug1.GND
  N1: J1.pin2, Q2.emitter
  N2: U1.VCC#1, Power_plug1.VCC, Q2.collector
  N3: U1.DIN, Mod2.GPIO26
  N4: U1.GND#4, U1.GND#7, U3.GND
  N5: U1.VCC#5, U3.VCC
  N6: U1.DOUT, U3.DIN
  N7: Mod2.GPIO19, Q2.base
  N8: Mod2.CAMERA, J2.camera

custom parts:
  WS2812 RGB LED matrix 1x8: WS2812 matrix 1x8
  Raspberry Pi 4B: The RPi4B, a faster version of the awesome Raspberry Pi 3 ARM Board with 40 pin gpio. Ready for special Raspberry Pi B+ and RPi2 Hat (Hardware attached (on) top) new features: The most surprising change for the Pi 4B is that it is available with three different amounts of fast DDR4 SDRAM memory; 1GB, 2GB, or 4GB. Combined with a newer 1.5GHz quad-core processor, the Pi 4B can run larger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
  Dagu DGServo 9g header connector (female): Dagu DGServo 9g header connector (female) This part represents the header plug found on the DGServo 9g. It is based on the standard female header, but is labelled to clearly indicate the ground, Vcc and pulse pins in schematic view. To use it, simply plug this part onto whichever header pins you are using, then attach the wires from a DGServo 9g part to the back of it. In schematic view,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
